# Fritzing sketch POPPY_Box (saved by Fritzing 0.8.7b)
circuit board: 9.74305cm x 5.6043cm
breadboards: 2

parts:
  Part1 = Arduino Uno (Rev3)
  U1 = POT [package=alps_pot]
  U2 = POT [package=alps_pot]
  S1 = Round Pushbutton
  S2 = Round Pushbutton

nets:
  N1: Part1.A0, U2.S
  N2: Part1.A1, U1.S
  N3: Part1.5V, S1.leg0, S2.leg1
  N4: Part1.GND, U1.A, U2.E
  N5: U1.E, S1.leg1
  N6: U2.A, S2.leg0
