# Fritzing sketch POPPY_Keyboard (saved by Fritzing 0.8.7b)
breadboards: 1

parts:
  Part1 = Arduino Uno (Rev3)
  IC1 = SELECTOR_MULTIPLEXER [package=dil16]
  S1 = Pushbutton [package="[THT]"]
  S2 = Pushbutton [package="[THT]"]
  S3 = Pushbutton [package="[THT]"]
  S4 = Pushbutton [package="[THT]"]
  S5 = Pushbutton [package="[THT]"]
  S6 = Pushbutton [package="[THT]"]
  S7 = Pushbutton [package="[THT]"]
  S8 = Pushbutton [package="[THT]"]

nets:
  N1: Part1.A0, IC1.A_3A
  N2: Part1.A1, IC1.A_3B
  N3: Part1.A2, IC1.A_3Y
  N4: Part1.D13/SCK, IC1.A_1B
  N5: Part1.5V, IC1.P_VCC, S1.Pin_3, S1.Pin_4, S2.Pin_3, S2.Pin_4, S3.Pin_3, S3.Pin_4, S4.Pin_3, S4.Pin_4, S5.Pin_3, S5.Pin_4, S6.Pin_3, S6.Pin_4, S7.Pin_3, S7.Pin_4, S8.Pin_3, S8.Pin_4
  N6: Part1.GND, IC1.A_2B, IC1.A_2Y, IC1.P_GND
  N7: IC1.A_!A!_B, S5.Pin_1, S5.Pin_2
  N8: IC1.A_1A, S7.Pin_1, S7.Pin_2
  N9: IC1.A_1Y, S8.Pin_1, S8.Pin_2
  N10: IC1.A_2A, S6.Pin_1, S6.Pin_2
  N11: IC1.A_4Y, S4.Pin_1, S4.Pin_2
  N12: IC1.A_4B, S1.Pin_1, S1.Pin_2
  N13: IC1.A_4A, S2.Pin_1, S2.Pin_2
  N14: IC1.A_G, S3.Pin_1, S3.Pin_2
